# Fritzing sketch rpi-ballotbox (saved by Fritzing 0.9.2b)
breadboards: 3

parts:
  Switching_regulator = Voltage Regulator - 5V [part_number=PT78ST105H package="TO220 [THT]"]
  IC1 = L293D [package=THT]
  D1 = Rectifier Diode [part_number=1N4001 package="300 mil [THT]"]
  D2 = Rectifier Diode [part_number=1N4001 package="300 mil [THT]"]
  D3 = Rectifier Diode [part_number=1N4001 package="300 mil [THT]"]
  D4 = Rectifier Diode [part_number=1N4001 package="300 mil [THT]"]
  2A = Fuse with Handler [part_number=Htc-15m]
  Power_button = Pushbutton [package=THT]
  Feed_motor_sensor = PHOTOTRANSISTOR REFLECTIVE OBJECT SENSOR [part_number="HP J110a" package=qrb1114-side]
  R1 = Resistor [tolerance=±5% resistance=220 package=THT]
  R2 = Resistor [tolerance=±5% resistance=7.5k package=THT]
  Diverter_servo = Basic Servo [part_number="Futaba S3003"]
  Paper_sensor = PHOTOTRANSISTOR REFLECTIVE OBJECT SENSOR [package=qrb1114-side]
  Raspberry_Pi2 = Raspberry Pi 2
  R3 = Resistor [tolerance=±5% resistance=220 package=THT]
  R4 = Resistor [tolerance=±5% resistance=1k package=THT]
  Q1 = NPN-Transistor [part_number=2N2222A package="TO92 [THT]"]
  R5 = Resistor [tolerance=±5% resistance=120k package=THT]
  Scanner_switch = male pin header, 2 pins [form="♂ (male)"]
  Sheet_feeder = DC Motor [part_number="HP J110a"]
  12Vdc_adapter = Power Jack [package=power_jack_pth_lock]
  C1 = Electrolytic Capacitor [capacitance=0.1mF package="100 mil [THT, electrolytic]"]
  C2 = Electrolytic Capacitor [capacitance=1µF package="100 mil [THT, electrolytic]"]

nets (from the schematic view):
  N1: Switching_regulator.input_voltage, 2A.Connector2, C2.+
  GND: Switching_regulator.GND, IC1.0V, D3.anode, D4.anode, Power_button.leg1, Feed_motor_sensor.E, Feed_motor_sensor.K, Diverter_servo.gnd, Raspberry_Pi2.GND, R3.Pin_0, R4.Pin_0, 12Vdc_adapter.GND, 12Vdc_adapter.GNDBREAK, C1.-, C2.-
  VCC: Switching_regulator.output_voltage, IC1.+V, Diverter_servo.vcc, Raspberry_Pi2.5V, C1.+
  N2: IC1.Enable_1, Raspberry_Pi2.GPIO17
  N3: IC1.In_1, Raspberry_Pi2.GPIO27
  N4: IC1.Out_1_(_Controlled_by_Enable_1_), D2.anode, D4.cathode, Sheet_feeder.pin_2
  N5: IC1.Out_2_(_Controlled_by_Enable_1_), D1.anode, D3.cathode, Sheet_feeder.pin_1
  N6: IC1.In_2, Raspberry_Pi2.GPIO22
  N7: IC1.+Vmotor, D1.cathode, D2.cathode, 2A.Connector1, 12Vdc_adapter.PWR
  N8: Power_button.leg0, Raspberry_Pi2.GPIO3
  N9: Feed_motor_sensor.A, R1.Pin_1
  N10: Feed_motor_sensor.C, R2.Pin_1, Raspberry_Pi2.GPIO23
  3V3: R1.Pin_0, R2.Pin_0, Paper_sensor.A, Paper_sensor.C, Raspberry_Pi2.3v3, Raspberry_Pi2.3V3
  N11: Diverter_servo.pulse, Raspberry_Pi2.GPIO18
  N12: Paper_sensor.E, Raspberry_Pi2.GPIO24, R4.Pin_1
  N13: Paper_sensor.K, R3.Pin_1
  N14: Raspberry_Pi2.GPIO25, R5.Pin_0
  N15: Q1.E, Scanner_switch.pin2
  N16: Q1.B, R5.Pin_1
  N17: Q1.C, Scanner_switch.pin1
